// Logisim project cpu.circ as structural Verilog: 2 circuits, main circuit main
module main (
  input  [31:0] INSTRUCTION,
  input  CLOCK,
  output [31:0] PROGRAM_COUNTER,
  output [31:0] ra,
  output [31:0] sp,
  output [31:0] t0,
  output [31:0] t1,
  output [31:0] t2,
  output [31:0] s0,
  output [31:0] s1,
  output [31:0] a0
);

  wire DMEM_p1, DMEM_p6, DMEM_p8;
  wire [31:0] adder_1_out, Arithmetic_Logic_Unit_result, bit_extender_1_out, DMEM_p10, multiplexer_1_out,
       multiplexer_2_out, RegFile_read_data_1, RegFile_read_data_2, register_1_q;

  Adder #(.width(32)) adder_1 (.a(PROGRAM_COUNTER), .b(32'h4), .out(adder_1_out));  // open: cin, cout
  Register #(.width(32)) PC (.D(adder_1_out), .clk(CLOCK), .Q(PROGRAM_COUNTER));  // open: en, clr
  Register #(.width(32)) register_1 (.D(INSTRUCTION), .en(1'b1), .clk(CLOCK), .Q(register_1_q));  // open: clr
  assign bit_extender_1_out = {{20{1'b0}}, register_1_q[31:20]};  // Bit_Extender bit_extender_1
  regfile_main RegFile (
    .rs2(register_1_q[24:20]), .rd(register_1_q[11:7]), .Read_Data_1(RegFile_read_data_1),
    .Read_Data_2(RegFile_read_data_2), .ra(ra), .sp(sp), .t0(t0), .t1(t1), .t2(t2), .s0(s0), .s1(s1),
    .a0(a0), .rs1(register_1_q[19:15]), .Write_Data(Arithmetic_Logic_Unit_result), .RegWEn(1'b1), .clk(CLOCK));
  Multiplexer #(.width(32), .enable("false")) multiplexer_1 (
    .in0(RegFile_read_data_1), .in1(PROGRAM_COUNTER), .out(multiplexer_1_out), .sel(1'b0));
  Multiplexer #(.width(32), .enable("false")) multiplexer_2 (
    .in0(RegFile_read_data_2), .in1(bit_extender_1_out), .out(multiplexer_2_out), .sel(1'b1));
  alu Arithmetic_Logic_Unit (
    .B(multiplexer_2_out), .Result(Arithmetic_Logic_Unit_result), .A(multiplexer_1_out), .ALUSel(4'b0000));
  // mem_main DMEM: pin names not known; wires that end beside it: DMEM_p1, Arithmetic_Logic_Unit_result, RegFile_read_data_2, DMEM_p1, CLOCK, DMEM_p6, DMEM_p6, DMEM_p8, 1'b0, DMEM_p10
  Multiplexer #(.select(2), .width(32), .enable("false")) multiplexer_3 (
    .in1(Arithmetic_Logic_Unit_result), .in2(DMEM_p10));  // open: in0, in3, out, sel

  // Other names for the same wires on the sheet: clk = CLOCK

  // Notes on the sheet:
  //   Output
  //   IMEM (do **NOT** move this)
  //   Inputs
  //   Inputs/Outputs for testing. Do **NOT** move these.
endmodule

module control_module (
  input  [31:0] Instruction_32,
  output BrEq,
  output BrLt,
  output PCSel,
  output ImmSel,
  output BrUn,
  output ASel,
  output BSel,
  output ALUSel,
  output MemRW,
  output RegWEn,
  output WBSel
);
endmodule
